// Logisim project Programa_Principal.circ as structural Verilog
module ALU_1bit (
  input  Cin,
  input  Inversor,
  input  B,
  input  A,
  input  [1:0] Code,
  output S,
  output Cout
);

  wire adder_1_cout, adder_1_out, and_1_out, or_1_out, xor_1_out;

  and and_1 (and_1_out, A, B);
  or or_1 (or_1_out, A, B);
  Adder #(.width(1)) adder_1 (.a(A), .b(xor_1_out), .out(adder_1_out), .cin(Cin), .cout(adder_1_cout));
  xor xor_1 (xor_1_out, B, Inversor);
  Multiplexer #(.select(2)) multiplexer_1 (
    .in0(and_1_out), .in1(or_1_out), .in2(adder_1_out), .out(S), .sel(Code));  // open: in3
endmodule

module ALU_8bits (
  input  in_1,
  input  [1:0] in_2,
  input  b0,
  input  a0,
  input  in_5,
  input  in_6,
  input  in_7,
  input  in_8,
  input  in_9,
  input  in_10,
  input  in_11,
  input  in_12,
  input  in_13,
  input  in_14,
  input  in_15,
  input  in_16,
  input  in_17,
  input  in_18
);

  wire ALU_0_cout, alu_1bit_1_cout, alu_1bit_2_cout, alu_1bit_3_cout, alu_1bit_4_cout, alu_1bit_5_cout,
       alu_1bit_6_cout, alu_1bit_7_cout;

  ALU_1bit ALU_0 (.Cin(in_1), .Inversor(in_1), .B(b0), .A(a0), .Code(in_2), .Cout(ALU_0_cout));  // open: S
  ALU_1bit alu_1bit_1 (
    .Cin(ALU_0_cout), .Inversor(in_1), .B(in_5), .A(in_6), .Code(in_2), .Cout(alu_1bit_1_cout));  // open: S
  ALU_1bit alu_1bit_2 (
    .Cin(alu_1bit_1_cout), .Inversor(in_1), .B(in_7), .A(in_8), .Code(in_2), .Cout(alu_1bit_2_cout));  // open: S
  ALU_1bit alu_1bit_3 (
    .Cin(alu_1bit_2_cout), .Inversor(in_1), .B(in_9), .A(in_10), .Code(in_2), .Cout(alu_1bit_3_cout));  // open: S
  ALU_1bit alu_1bit_4 (
    .Cin(alu_1bit_3_cout), .Inversor(in_1), .B(in_11), .A(in_12), .Code(in_2), .Cout(alu_1bit_4_cout));  // open: S
  ALU_1bit alu_1bit_5 (
    .Cin(alu_1bit_4_cout), .Inversor(in_1), .B(in_13), .A(in_14), .Code(in_2), .Cout(alu_1bit_5_cout));  // open: S
  ALU_1bit alu_1bit_6 (
    .Cin(alu_1bit_5_cout), .Inversor(in_1), .B(in_15), .A(in_16), .Code(in_2), .Cout(alu_1bit_6_cout));  // open: S
  ALU_1bit alu_1bit_7 (
    .Cin(alu_1bit_6_cout), .Inversor(in_1), .B(in_17), .A(in_18), .Code(in_2), .Cout(alu_1bit_7_cout));  // open: S
endmodule
